# Fritzing sketch Proyecto (saved by Fritzing 0.8.7b)
circuit board: 8.46667cm x 5.64444cm
breadboards: 1

parts:
  Parte1 = Arduino Uno (Rev3)
  DS1 = DS18B20 1-Wire Temperature Sensor [part_number=DS18B20]
  U1 = ESP8266 WiFi Module [part_number=ESP8266]
  LCM1602_IIC1 = LCM1602 IIC [part_number="LCM1602 IIC" chip_label="LCM1602 IIC" package="DIP (Dual Inline) [THT]"]
  R2 = Resistor [package="2512 [SMD]"]

nets:
  N1: Parte1.A4/SDA, LCM1602_IIC1.SDA
  N2: Parte1.A5/SCL, LCM1602_IIC1.SCL
  N3: Parte1.D9_PWM, DS1.DQ, R2.Pin_0
  GND: Parte1.GND, DS1.GND, U1.GND, LCM1602_IIC1.GND
  N4: Parte1.D2, U1.TXD
  N5: Parte1.D3_PWM, U1.RXD
  3V3: Parte1.3V3, U1.VCC, U1.CH_PD
  5V: Parte1.5V, DS1.VDD, LCM1602_IIC1.VCC, R2.Pin_1

notes:
  5 Ohm

custom parts:
  ESP8266 WiFi Module: Generic WiFi Module based on the ESP8266 with onboard PCB antenna and UART communications
  LCM1602 IIC: I2C-Module to use a 1602 or 2004 LCD on with the wire.h libory Serial LCD Modul
